// Logisim project Mantissa Logisim.circ as structural Verilog: 1 circuit, main circuit main
module main (
  input  [5:0] Original,
  input  in_2,
  input  in_3,
  input  in_4
);

  wire and_1_out, and_2_out, and_3_out, and_4_out, clock_1_out, controlled_buffer_1_out,
       controlled_buffer_2_out, controlled_buffer_3_out, controlled_buffer_4_out, controlled_buffer_5_out,
       controlled_buffer_6_out, Mantissa_out, or_1_out, or_2_out, or_3_out, or_4_out, or_5_out, or_6_out,
       or_7_out, or_8_out, or_9_out, or_10_out, register_1_q, register_2_q, register_3_q, register_4_q,
       register_5_q;
  wire [5:0] Mantissa_q5;

  Clock clock_1 (.out(clock_1_out));
  and and_1 (and_1_out, Original[5], or_2_out);
  or or_1 (or_1_out, Original[4], and_1_out);
  assign controlled_buffer_1_out = Original[5] ? Original[5] : 1'bz;  // Controlled_Buffer controlled_buffer_1
  assign controlled_buffer_2_out = or_1_out ? Original[4] : 1'bz;  // Controlled_Buffer controlled_buffer_2
  assign controlled_buffer_3_out = or_4_out ? Original[3] : 1'bz;  // Controlled_Buffer controlled_buffer_3
  assign controlled_buffer_4_out = or_8_out ? Original[2] : 1'bz;  // Controlled_Buffer controlled_buffer_4
  assign controlled_buffer_5_out = or_10_out ? Original[1] : 1'bz;  // Controlled_Buffer controlled_buffer_5
  Shift_Register #(.length(6)) Mantissa (
    .shift(in_3), .clk(clock_1_out), .out(Mantissa_out), .load(in_2), .clr(in_4),
    .d0(controlled_buffer_1_out), .q0(Mantissa_q5[5]), .d1(controlled_buffer_2_out), .q1(Mantissa_q5[4]),
    .d2(controlled_buffer_3_out), .q2(Mantissa_q5[3]), .d3(controlled_buffer_4_out), .q3(Mantissa_q5[2]),
    .d4(controlled_buffer_5_out), .q4(Mantissa_q5[1]), .d5(controlled_buffer_6_out), .q5(Mantissa_q5[0]));  // open: in
  or or_2 (or_2_out, Original[3], Original[2], Original[1], Original[0]);
  or or_3 (or_3_out, Original[5], Original[4]);
  and and_2 (and_2_out, or_3_out, or_5_out);
  or or_4 (or_4_out, Original[3], and_2_out);
  assign controlled_buffer_6_out = Original[0] ? Original[0] : 1'bz;  // Controlled_Buffer controlled_buffer_6
  or or_5 (or_5_out, Original[2], Original[1], Original[0]);
  or or_6 (or_6_out, Original[5], Original[4], Original[3]);
  or or_7 (or_7_out, Original[1], Original[0]);
  and and_3 (and_3_out, or_6_out, or_7_out);
  or or_8 (or_8_out, Original[2], and_3_out);
  Register #(.width(1)) register_1 (.D(Mantissa_out), .Q(register_1_q), .clk(clock_1_out), .clr(in_4));  // open: en
  or or_9 (or_9_out, Original[5], Original[4], Original[3], Original[2]);
  and and_4 (and_4_out, or_9_out, Original[0]);
  or or_10 (or_10_out, Original[1], and_4_out);
  Register #(.width(1)) register_2 (.D(register_3_q), .Q(register_2_q), .clk(clock_1_out), .clr(in_4));  // open: en
  Register #(.width(1)) register_3 (.D(register_1_q), .Q(register_3_q), .clk(clock_1_out), .clr(in_4));  // open: en
  Register #(.width(1)) register_4 (.D(register_5_q), .Q(register_4_q), .clk(clock_1_out), .clr(in_4));  // open: en
  Register #(.width(1)) register_5 (.D(register_2_q), .Q(register_5_q), .clk(clock_1_out), .clr(in_4));  // open: en
  Register #(.width(1)) register_6 (.D(register_4_q), .clk(clock_1_out), .clr(in_4));  // open: en, Q
endmodule
